// Logisim project CPU.circ as structural Verilog: 2 circuits, main circuit CLK
module CLK (
  input  E,
  output P
);

  wire and_1_out, clock_1_out, not_1_out;

  Clock clock_1 (.out(clock_1_out));
  and and_1 (and_1_out, E, clock_1_out);
  not not_1 (not_1_out, and_1_out);
  and and_2 (P, and_1_out, not_1_out);
endmodule

module MAIN (
);

  wire clk_1_p, j_k_ff_1_q;

  CLK clk_1 (.E(1'b1), .P(clk_1_p));
  J_K_Flip_Flop j_k_ff_1 (.J(1'b1), .K(1'b1), .clk(clk_1_p), .Q(j_k_ff_1_q));  // open: Qn, preset, reset
endmodule
